# Fritzing sketch MotorDriver (saved by Fritzing 0.9.3b)
circuit board: 6.5cm x 4.54628cm
breadboards: 1

parts:
  Teensy_3_1 = Teensy 3.1
  Part1 = Motor Driver 1A Dual TB6612FNG
  M2 = Screw terminal - 2 pins [package=THT]
  M1 = Screw terminal - 2 pins [package=THT]
  VCC = Screw terminal - 2 pins [package=THT]
  VBAT = Screw terminal - 2 pins [package=THT]

nets:
  GND: Teensy_3_1.GND, Part1.GND, VCC.pin2, VBAT.pin2
  N1: Teensy_3_1.D2, Part1.AIN1
  N2: Teensy_3_1.D3, Part1.AIN2
  N3: Teensy_3_1.D4, Part1.BIN1
  N4: Teensy_3_1.D5, Part1.BIN2
  N5: Teensy_3_1.A8/D22, Part1.PWMA
  N6: Teensy_3_1.A9/D23, Part1.PWMB
  VIN: Teensy_3_1.Vin, Part1.VCC, Part1.STBY, VCC.pin1
  N7: Part1.B01, M2.pin2
  N8: Part1.B02, M2.pin1
  N9: Part1.A02, M1.pin2
  N10: Part1.A01, M1.pin1
  N11: Part1.VM, VBAT.pin1
